# Fritzing sketch bluetooth-car-speed-control-ultrasonic (saved by Fritzing 0.9.3b)

parts:
  S1 = H-Bridge with L298N
  M3 = DC Motor
  M4 = DC Motor
  Parça1 = Arduino Uno (Rev3)
  Parça2 = Bluetooth HC-05 Macho
  VCC1 = 4 x AAA Battery Mount
  M1 = DC Motor
  M2 = DC Motor
  VCC2 = Battery
  hc-sr1 = hc-sr04

nets:
  N1: S1.12V, VCC2.+
  N2: S1.GND, VCC2.-
  N3: S1.ENA, Parça1.D5_PWM
  N4: S1.IN1, Parça1.D8
  N5: S1.IN2, Parça1.D9_PWM
  N6: S1.IN3, Parça1.D10_PWM/SS
  N7: S1.IN4, Parça1.D11_PWM/MOSI
  N8: S1.ENB, Parça1.D6_PWM
  N9: M3.pin_1, M4.pin_1
  N10: M3.pin_2, M4.pin_2
  N11: Parça1.D12/MISO, hc-sr1.Trig
  N12: Parça1.D13/SCK, hc-sr1.Echo
  N13: Parça1.D2, Parça2.RXD
  N14: Parça1.D3_PWM, Parça2.TXD
  3V3: Parça1.3V3, Parça2.VCC
  5V: Parça1.5V, hc-sr1.VCC
  GND: Parça1.GND, Parça2.GND, VCC1.-
  N15: Parça1.VIN, VCC1.+
  N16: M1.pin_1, M2.pin_1
  N17: M1.pin_2, M2.pin_2

notes:
  MOTOR-A (MA)
  MOTOR-B (MB)
  MAA
  MAK
  MBK
  MBA
  MAHiz
  MBHiz
  DC 6v

custom parts:
  H-Bridge with L298N: h-bridge
  Battery: Your standard 2x 18650 battery pack (7,4 Volts)
