# Fritzing sketch butonUygulama (saved by Fritzing 0.9.3b)
breadboards: 1

parts:
  Parça1 = Arduino Uno (Rev3) - ICSP
  R1 = Resistor [tolerance=±5% resistance=220 package=THT]  # not connected
  LED1 = LED - 5mm [color="Red (633nm)" package="5 mm [THT]"]
  R2 = Resistor [tolerance=±5% resistance=10k package=THT]
  S1 = Pushbutton [package="[THT]"]

nets:
  N1: Parça1.D10_PWM/SS, LED1.anode
  N2: Parça1.GND, R2.Pin_1
  N3: Parça1.D2, R2.Pin_0, S1.Pin_1, S1.Pin_2
  N4: Parça1.5V, S1.Pin_3, S1.Pin_4
