# Fritzing sketch butonUygulama1 (saved by Fritzing 0.9.3b)
breadboards: 1

parts:
  S1 = Pushbutton [package="[THT]"]
  Parça1 = Arduino Uno (Rev3) - ICSP

nets:
  N1: S1.Pin_1, S1.Pin_2
  N2: S1.Pin_3, S1.Pin_4, Parça1.D2, Parça1.GND
