# Fritzing sketch arduino_uno_10_led_button(interrupt) (saved by Fritzing 0.9.3b)
breadboards: 1

parts:
  Parça1 = Arduino Uno (Rev3)
  LED1 = smd LED [color="Red (633nm)" package="0603 [SMD]"]
  LED2 = smd LED [color="Red (633nm)" package="0603 [SMD]"]
  LED3 = smd LED [color="Red (633nm)" package="0603 [SMD]"]
  LED4 = smd LED [color="Red (633nm)" package="0603 [SMD]"]
  LED5 = smd LED [color="Red (633nm)" package="0603 [SMD]"]
  LED6 = smd LED [color="Red (633nm)" package="0603 [SMD]"]
  LED7 = smd LED [color="Red (633nm)" package="0603 [SMD]"]
  LED8 = smd LED [color="Red (633nm)" package="0603 [SMD]"]
  LED9 = smd LED [color="Red (633nm)" package="0603 [SMD]"]
  LED10 = smd LED [color="Red (633nm)" package="0603 [SMD]"]
  S1 = Pushbutton [package="[THT]"]

nets:
  N1: Parça1.D8, LED6.anode
  N2: Parça1.D9_PWM, LED5.anode
  N3: Parça1.D10_PWM/SS, LED4.anode
  N4: Parça1.D11_PWM/MOSI, LED3.anode
  N5: Parça1.D12/MISO, LED2.anode
  N6: Parça1.D13/SCK, LED1.anode
  N7: Parça1.GND, Parça1.D3_PWM, LED1.cathode, LED2.cathode, LED3.cathode, LED4.cathode, LED5.cathode, LED6.cathode, LED7.cathode, LED8.cathode, LED9.cathode, LED10.cathode, S1.Pin_1, S1.Pin_2, S1.Pin_3, S1.Pin_4
  N8: Parça1.D4, LED10.anode
  N9: Parça1.D5_PWM, LED9.anode
  N10: Parça1.D6_PWM, LED8.anode
  N11: Parça1.D7, LED7.anode
