# Fritzing sketch Fritzing_devre_semasi (saved by Fritzing 0.9.3b)

parts:
  Parça1 = Bluetooth HC-05 Macho
  Parça2 = Arduino Uno (Rev3) - ICSP

nets:
  N1: Parça1.TXD, Parça2.D10_PWM/SS
  N2: Parça1.RXD, Parça2.D11_PWM/MOSI
  N3: Parça1.VCC, Parça2.D6_PWM
  GND: Parça1.GND, Parça2.GND

notes:
  PIO11 / Pin34
