# Fritzing sketch hc05_level_shifter (saved by Fritzing 0.9.3b)
breadboards: 1

parts:
  Parça1 = Arduino Ethernet Shield (Rev3)
  Parça2 = Bluetooth HC-05 Macho
  R1 = Resistor [tolerance=±5% resistance=1k package="0603 [SMD]"]
  R2 = Resistor [tolerance=±5% resistance=2.2k package="0603 [SMD]"]

nets:
  N1: Parça1.ETH_CS, Parça2.TXD
  N2: Parça1.PWM_D11, R1.Pin_1
  5V: Parça1.5V, Parça2.VCC
  GND: Parça1.GND, Parça2.GND
  N3: Parça2.RXD, R1.Pin_0, R2.Pin_1
